// Logisim project ping-pong.circ as structural Verilog: 16 circuits, main circuit PING_PONG
module movePoint (
  input  [6:0] Keyboard,
  output [3:0] out_2,
  output [3:0] out_3,
  output [3:0] out_4,
  output [31:0] out_5,
  output [31:0] out_6,
  output [31:0] out_7,
  output [31:0] out_8,
  output [31:0] out_9,
  output [31:0] out_10,
  output [31:0] out_11,
  output [31:0] out_12,
  output [31:0] out_13,
  output [31:0] out_14,
  output [31:0] out_15,
  output [31:0] out_16,
  output [31:0] out_17,
  output [31:0] out_18,
  output [31:0] out_19,
  output [31:0] out_20,
  output [31:0] out_21,
  output [31:0] out_22,
  output [31:0] out_23,
  output [31:0] out_24,
  output [31:0] out_25,
  output [31:0] out_26,
  output [31:0] out_27,
  output [31:0] out_28,
  output [31:0] out_29,
  output [31:0] out_30,
  output [31:0] out_31,
  output [31:0] out_32,
  output [31:0] out_33,
  output [31:0] out_34,
  output [31:0] out_35,
  output [31:0] out_36,
  output [3:0] out_37,
  output [3:0] out_38,
  output [3:0] out_39,
  output [3:0] sec_0,
  output [3:0] sec_1,
  output [3:0] min_0,
  output [3:0] min_1,
  output keyboard_power
);

  wire and_1_out, and_2_out, and_5_out, and_6_out, and_7_out, and_8_out, and_9_out, and_10_out, and_11_out,
       and_12_out, bot_enabled, comparator_5_eq, comparator_6_eq, comparator_7_eq, comparator_8_eq,
       comparator_10_eq, comparator_12_eq, comparator_14_eq, comparator_15_eq, comparator_16_eq,
       comparator_17_eq, comparator_18_eq, comparator_19_eq, comparator_20_eq, comparator_21_eq,
       comparator_22_eq, d_ff_3_q, fail1, fail2, frequency_divider_1_out, frequency_divider_2_out, gameover,
       is_ball_16, isDown, isLeft, l_button, l_pressed, lose, not_1_out, not_2_out, not_3_out, not_4_out,
       not_5_out, not_6_out, not_7_out, not_8_out, not_9_out, not_10_out, not_11_out, not_12_out, not_13_out,
       not_14_out, not_15_out, not_16_out, not_17_out, not_18_out, not_19_out, o_button, o_pressed, or_1_out,
       or_2_out, or_3_out, or_4_out, or_5_out, or_6_out, or_8_out, or_9_out, or_11_out, or_12_out, or_25_out,
       or_27_out, or_28_out, P, pause, playing, power, pull_resistor_2_node, r1, r2, rest_pressed, restart,
       s_button, s_pressed, space_pr, space_pressed, swap_x_dir_left_r_to_left, swap_x_dir_right_r_to_right,
       swap_x_direction_left_wall, swap_x_direction_right_wall, t_ff_1_q, transistor_1_out, transistor_3_out,
       w_button, w_pressed, win;
  wire [2:0] aoa;
  wire [3:0] bit_extender_1_out, stopwatch2hz_2_min_0, stopwatch2hz_2_min_1, stopwatch2hz_2_sec_0,
       stopwatch2hz_2_sec_1;
  wire [4:0] counter_3_q, counter_4_q, dmx_x_cord, middle_rocket_pixel_left, multiplexer_13_out,
       multiplexer_15_out, prev_val;
  wire [6:0] keyboard_t, test_keyboard;
  wire [7:0] multiplexer_14_out, multiplexer_16_out, multiplexer_51_out, p1_score_bin, p2_score_bin;
  wire [30:1] decoder_2_out0, decoder_3_out0;
  wire [31:0] bot, bot_borris_1_new_y, cord1, cord2, cord11, cord22, D0, D1, D3, D5, D6, D7, D8, D9, D10,
       D11, D12, D13, D14, D15, D16, D17, D18, D19, D20, D21, D22, D23, D24, D25, D26, D28, D30, D31,
       demultiplexer_1_out3, demultiplexer_1_out28, dmx_y_cord, lw4, lw5, lw6, lw7, lw8, lw9, lw10, lw11,
       lw12, lw13, lw14, lw15, or_13_out, or_15_out, player1, player2, racket2, shifter_1_out, shifter_2_out,
       shifter_3_out, shifter_4_out, shifter_5_out, shifter_6_out, y_pause_cord;

  or or_1 (or_1_out, space_pressed, rest_pressed);
  or or_2 (or_2_out, space_pressed, rest_pressed);
  Multiplexer #(.width(32)) multiplexer_1 (.in0({32{1'b0}}), .in1(32'h60000), .out(lw4), .sel(win));  // open: en
  Multiplexer #(.width(32)) multiplexer_2 (.in0({32{1'b0}}), .in1(32'h90000), .out(lw5), .sel(win));  // open: en
  Multiplexer #(.width(32)) multiplexer_3 (.in0({32{1'b0}}), .in1(32'h9c000), .out(lw6), .sel(win));  // open: en
  Multiplexer #(.width(32)) multiplexer_4 (.in0({32{1'b0}}), .in1(32'h63000), .out(lw7), .sel(win));  // open: en
  Multiplexer #(.width(32)) multiplexer_5 (.in0(32'h7c000), .in1(32'h10c00), .out(lw8), .sel(win));  // open: en
  Multiplexer #(.width(32)) multiplexer_6 (.in0(32'h382000), .in1(32'h10200), .out(lw9), .sel(win));  // open: en
  Multiplexer #(.width(32)) multiplexer_7 (.in0(32'h439000), .in1(32'h8200), .out(lw10), .sel(win));  // open: en
  Multiplexer #(.width(32)) multiplexer_8 (.in0(32'h87d000), .in1(32'h8200), .out(lw11), .sel(win));  // open: en
  Multiplexer #(.width(32)) multiplexer_9 (.in0(32'h87cf00), .in1(32'h4200), .out(lw12), .sel(win));  // open: en
  Multiplexer #(.width(32)) multiplexer_10 (.in0(32'h107c080), .in1(32'h18200), .out(lw13), .sel(win));  // open: en
  Multiplexer #(.width(32)) multiplexer_11 (.in0(32'h1038080), .in1(32'h360200), .out(lw14), .sel(win));  // open: en
  Multiplexer #(.width(32)) multiplexer_12 (.in0(32'h1001880), .in1(32'h480200), .out(lw15), .sel(win));  // open: en
  Multiplexer #(.width(5)) multiplexer_13 (
    .in0(prev_val), .in1(middle_rocket_pixel_left), .out(multiplexer_13_out), .sel(or_1_out));  // open: en
  Multiplexer #(.select(3), .width(8)) multiplexer_14 (
    .in0(8'hc), .in1(8'h8), .in2(8'h6), .in3(8'h4), .in4(8'h3), .in5(8'h2), .out(multiplexer_14_out),
    .sel(aoa));  // open: in6, in7, en
  Multiplexer #(.width(5)) multiplexer_15 (
    .in0(dmx_x_cord), .in1(5'b00100), .out(multiplexer_15_out), .sel(or_2_out));  // open: en
  Multiplexer #(.select(3), .width(8)) multiplexer_16 (
    .in0(8'h2), .in1(8'h3), .in2(8'h4), .in3(8'h6), .in4(8'h8), .in5(8'hc), .out(multiplexer_16_out),
    .sel(aoa));  // open: in6, in7, en
  or or_3 (or_3_out, isDown, or_1_out);
  frequency_divider frequency_divider_1 (
    .IN(power), .OUT(frequency_divider_1_out), .n(multiplexer_14_out));  // open: _0
  or or_4 (or_4_out, isLeft, or_2_out);
  frequency_divider frequency_divider_2 (
    .IN(power), .OUT(frequency_divider_2_out), .n(multiplexer_16_out));  // open: _0
  Counter #(.width(5), .max('h1f)) counter_1 (
    .load(or_3_out), .D(multiplexer_13_out), .count(not_1_out), .Q(prev_val), .clk(frequency_divider_1_out),
    .clr(restart));  // open: carry
  not not_1 (not_1_out, or_1_out);
  Counter #(.width(5), .max('h1f)) counter_2 (
    .load(or_4_out), .D(multiplexer_15_out), .count(not_2_out), .Q(dmx_x_cord),
    .clk(frequency_divider_2_out), .clr(restart));  // open: carry
  not not_2 (not_2_out, or_2_out);
  Decoder #(.select(5)) decoder_1 (
    .out0(dmx_y_cord[0]), .out1(dmx_y_cord[1]), .out2(dmx_y_cord[2]), .out3(dmx_y_cord[3]),
    .out4(dmx_y_cord[4]), .out5(dmx_y_cord[5]), .out6(dmx_y_cord[6]), .out7(dmx_y_cord[7]),
    .out8(dmx_y_cord[8]), .out9(dmx_y_cord[9]), .out10(dmx_y_cord[10]), .out11(dmx_y_cord[11]),
    .out12(dmx_y_cord[12]), .out13(dmx_y_cord[13]), .out14(dmx_y_cord[14]), .out15(dmx_y_cord[15]),
    .out16(dmx_y_cord[16]), .out17(dmx_y_cord[17]), .out18(dmx_y_cord[18]), .out19(dmx_y_cord[19]),
    .out20(dmx_y_cord[20]), .out21(dmx_y_cord[21]), .out22(dmx_y_cord[22]), .out23(dmx_y_cord[23]),
    .out24(dmx_y_cord[24]), .out25(dmx_y_cord[25]), .out26(dmx_y_cord[26]), .out27(dmx_y_cord[27]),
    .out28(dmx_y_cord[28]), .out29(dmx_y_cord[29]), .out30(dmx_y_cord[30]), .out31(dmx_y_cord[31]),
    .sel(prev_val));  // open: en
  bot_borris bot_borris_1 (.New_Y(bot_borris_1_new_y));  // open: X, Y, Vx, Vy
  Multiplexer #(.width(32)) multiplexer_17 (.in0(player2), .in1(bot), .out(racket2), .sel(bot_enabled));  // open: en
  Multiplexer #(.select(2), .width(32), .enable("false")) multiplexer_18 (
    .in0(32'h6e3000), .in1(D12), .in2(lw12), .in3(D12), .out(out_17), .sel({pause, playing}));
  // Probe on keyboard_t
  // Probe on keyboard_t
  // Probe on keyboard_t
  // Probe on keyboard_t
  or or_5 (or_5_out, swap_x_direction_right_wall, swap_x_dir_left_r_to_left);
  or or_6 (or_6_out, swap_x_direction_left_wall, swap_x_dir_right_r_to_right);
  assign D3 = player1 | demultiplexer_1_out3;  // OR_Gate or_7, 32 bits wide
  Multiplexer #(.select(2), .width(32), .enable("false")) multiplexer_19 (
    .in0(32'h924400), .in1(D16), .in2(lw15), .in3(D16), .out(out_21), .sel({pause, playing}));
  Comparator #(.width(7)) comparator_1 (.a(keyboard_t), .b(7'b1110111), .eq(w_button));  // open: gt, lt
  Comparator #(.width(7)) comparator_2 (.a(keyboard_t), .b(7'b1110011), .eq(s_button));  // open: gt, lt
  Comparator #(.width(7)) comparator_3 (.a(keyboard_t), .b(7'b1101111), .eq(o_button));  // open: gt, lt
  Comparator #(.width(7)) comparator_4 (.a(keyboard_t), .b(7'b1101100), .eq(l_button));  // open: gt, lt
  D_Flip_Flop d_ff_1 (.Q(isLeft), .preset(or_5_out), .reset(or_6_out));  // open: clk, D, Qn, en
  Shifter #(.width(32)) shifter_1 (.in(dmx_y_cord), .\dist (5'b00001), .out(shifter_1_out));
  Shifter #(.width(32), .shift("lr")) shifter_2 (.in(dmx_y_cord), .\dist (5'b00001), .out(shifter_2_out));
  Multiplexer #(.select(2), .width(32), .enable("false")) multiplexer_20 (
    .in0({32{1'b0}}), .in1(D0), .in2({32{1'b0}}), .in3(D0), .out(out_5), .sel({pause, playing}));
  Multiplexer #(.select(2), .width(32), .enable("false")) multiplexer_21 (
    .in0(32'hfe3200), .in1(cord1), .in2(lw4), .in3(cord1), .out(out_9), .sel({pause, playing}));
  Multiplexer #(.select(2), .width(32), .enable("false")) multiplexer_22 (
    .in0({32{1'b0}}), .in1(D8), .in2(lw8), .in3(D8), .out(out_13), .sel({pause, playing}));
  Multiplexer #(.select(2), .width(32), .enable("false")) multiplexer_23 (
    .in0({32{1'b0}}), .in1(D13), .in2(lw13), .in3(D13), .out(out_18), .sel({pause, playing}));
  Multiplexer #(.select(2), .width(32), .enable("false")) multiplexer_24 (
    .in0(32'h922200), .in1(D20), .in2(lw11), .in3(D20), .out(out_25), .sel({pause, playing}));
  Multiplexer #(.select(2), .width(32), .enable("false")) multiplexer_25 (
    .in0(32'h647f00), .in1(D24), .in2(lw7), .in3(D24), .out(out_29), .sel({pause, playing}));
  Multiplexer #(.select(2), .width(32), .enable("false")) multiplexer_26 (
    .in0({32{1'b0}}), .in1(D28), .in2({32{1'b0}}), .in3(D28), .out(out_33), .sel({pause, playing}));
  or or_8 (or_8_out, l_button, restart);
  or or_9 (or_9_out, o_button, restart, l_button);
  D_Flip_Flop d_ff_2 (.Q(isDown), .preset(dmx_y_cord[31]), .reset(dmx_y_cord[0]));  // open: clk, D, Qn, en
  assign bot = shifter_1_out | dmx_y_cord | shifter_2_out;  // OR_Gate or_10, 32 bits wide
  Demultiplexer #(.select(5), .width(32)) demultiplexer_1 (
    .out0(D0), .out1(D1), .out2(cord11), .out3(demultiplexer_1_out3), .out4(cord1), .out5(D5), .out6(D6),
    .out7(D7), .out8(D8), .out9(D9), .out10(D10), .out11(D11), .out12(D12), .out13(D13), .out14(D14),
    .out15(D15), .out16(D16), .out17(D17), .out18(D18), .out19(D19), .out20(D20), .out21(D21), .out22(D22),
    .out23(D23), .out24(D24), .out25(D25), .out26(D26), .out27(cord2), .out28(demultiplexer_1_out28),
    .out29(cord22), .out30(D30), .out31(D31), .in(dmx_y_cord), .sel(dmx_x_cord));  // open: en
  or or_11 (or_11_out, s_button, restart);
  not not_3 (not_3_out, restart);
  or or_12 (or_12_out, w_button, restart, s_button);
  Counter #(.width(5), .max('h1d), .ongoal("stay")) counter_3 (
    .load(or_8_out), .D(5'b01111), .count(not_4_out), .Q(counter_3_q), .clk(or_9_out));  // open: carry, clr
  not not_4 (not_4_out, restart);
  Multiplexer #(.select(2), .width(32), .enable("false")) multiplexer_27 (
    .in0({32{1'b0}}), .in1(D1), .in2({32{1'b0}}), .in3(D1), .out(out_6), .sel({pause, playing}));
  Multiplexer #(.select(2), .width(32), .enable("false")) multiplexer_28 (
    .in0(32'h904900), .in1(D5), .in2(lw5), .in3(D5), .out(out_10), .sel({pause, playing}));
  Multiplexer #(.select(2), .width(32), .enable("false")) multiplexer_29 (
    .in0(32'hfe7f00), .in1(D9), .in2(lw9), .in3(D9), .out(out_14), .sel({pause, playing}));
  Multiplexer #(.select(2), .width(32), .enable("false")) multiplexer_30 (
    .in0(32'h923f00), .in1(D17), .in2(lw14), .in3(or_13_out), .out(out_22), .sel({pause, playing}));
  assign or_13_out = y_pause_cord | D17;  // OR_Gate or_13, 32 bits wide
  Multiplexer #(.select(2), .width(32), .enable("false")) multiplexer_31 (
    .in0(32'h924100), .in1(D21), .in2(lw10), .in3(D21), .out(out_26), .sel({pause, playing}));
  Multiplexer #(.select(2), .width(32), .enable("false")) multiplexer_32 (
    .in0(32'h924900), .in1(D25), .in2(lw6), .in3(D25), .out(out_30), .sel({pause, playing}));
  Multiplexer #(.select(2), .width(32), .enable("false")) multiplexer_33 (
    .in0({32{1'b0}}), .in1(cord22), .in2({32{1'b0}}), .in3(cord22), .out(out_34), .sel({pause, playing}));
  Counter #(.width(5), .max('h1d), .ongoal("stay")) counter_4 (
    .load(or_11_out), .D(5'b01111), .count(not_3_out), .Q(counter_4_q), .clk(or_12_out));  // open: carry, clr
  assign D28 = racket2 | demultiplexer_1_out28;  // OR_Gate or_14, 32 bits wide
  assign or_15_out = y_pause_cord | D14;  // OR_Gate or_15, 32 bits wide
  Decoder #(.select(5)) decoder_2 (
    .out0(decoder_2_out0[1]), .out1(decoder_2_out0[2]), .out2(decoder_2_out0[3]), .out3(decoder_2_out0[4]),
    .out4(decoder_2_out0[5]), .out5(decoder_2_out0[6]), .out6(decoder_2_out0[7]), .out7(decoder_2_out0[8]),
    .out8(decoder_2_out0[9]), .out9(decoder_2_out0[10]), .out10(decoder_2_out0[11]),
    .out11(decoder_2_out0[12]), .out12(decoder_2_out0[13]), .out13(decoder_2_out0[14]),
    .out14(decoder_2_out0[15]), .out15(decoder_2_out0[16]), .out16(decoder_2_out0[17]),
    .out17(decoder_2_out0[18]), .out18(decoder_2_out0[19]), .out19(decoder_2_out0[20]),
    .out20(decoder_2_out0[21]), .out21(decoder_2_out0[22]), .out22(decoder_2_out0[23]),
    .out23(decoder_2_out0[24]), .out24(decoder_2_out0[25]), .out25(decoder_2_out0[26]),
    .out26(decoder_2_out0[27]), .out27(decoder_2_out0[28]), .out28(decoder_2_out0[29]),
    .out29(decoder_2_out0[30]), .sel(counter_4_q));  // open: out30, out31, en
  Adder #(.width(5)) adder_1 (.a(counter_4_q), .b(5'b00001), .out(middle_rocket_pixel_left));  // open: cin, cout
  Decoder #(.select(5)) decoder_3 (
    .out0(decoder_3_out0[1]), .out1(decoder_3_out0[2]), .out2(decoder_3_out0[3]), .out3(decoder_3_out0[4]),
    .out4(decoder_3_out0[5]), .out5(decoder_3_out0[6]), .out6(decoder_3_out0[7]), .out7(decoder_3_out0[8]),
    .out8(decoder_3_out0[9]), .out9(decoder_3_out0[10]), .out10(decoder_3_out0[11]),
    .out11(decoder_3_out0[12]), .out12(decoder_3_out0[13]), .out13(decoder_3_out0[14]),
    .out14(decoder_3_out0[15]), .out15(decoder_3_out0[16]), .out16(decoder_3_out0[17]),
    .out17(decoder_3_out0[18]), .out18(decoder_3_out0[19]), .out19(decoder_3_out0[20]),
    .out20(decoder_3_out0[21]), .out21(decoder_3_out0[22]), .out22(decoder_3_out0[23]),
    .out23(decoder_3_out0[24]), .out24(decoder_3_out0[25]), .out25(decoder_3_out0[26]),
    .out26(decoder_3_out0[27]), .out27(decoder_3_out0[28]), .out28(decoder_3_out0[29]),
    .out29(decoder_3_out0[30]), .sel(counter_3_q));  // open: out30, out31, en
  // Probe on racket2
  // Probe on player1
  Multiplexer #(.select(2), .width(32), .enable("false")) multiplexer_34 (
    .in0({32{1'b0}}), .in1(cord11), .in2({32{1'b0}}), .in3(cord11), .out(out_7), .sel({pause, playing}));
  Multiplexer #(.select(2), .width(32), .enable("false")) multiplexer_35 (
    .in0(32'h904900), .in1(D6), .in2(lw6), .in3(D6), .out(out_11), .sel({pause, playing}));
  Multiplexer #(.select(2), .width(32), .enable("false")) multiplexer_36 (
    .in0(32'h904800), .in1(D10), .in2(lw10), .in3(D10), .out(out_15), .sel({pause, playing}));
  Multiplexer #(.select(2), .width(32), .enable("false")) multiplexer_37 (
    .in0(32'hfe3f00), .in1(D14), .in2(lw14), .in3(or_15_out), .out(out_19), .sel({pause, playing}));
  Multiplexer #(.select(2), .width(32), .enable("false")) multiplexer_38 (
    .in0({32{1'b0}}), .in1(D18), .in2(lw13), .in3(D18), .out(out_23), .sel({pause, playing}));
  Multiplexer #(.select(2), .width(32), .enable("false")) multiplexer_39 (
    .in0(32'h4c4100), .in1(D22), .in2(lw9), .in3(D22), .out(out_27), .sel({pause, playing}));
  Multiplexer #(.select(2), .width(32), .enable("false")) multiplexer_40 (
    .in0(32'h924900), .in1(D26), .in2(lw5), .in3(D26), .out(out_31), .sel({pause, playing}));
  Multiplexer #(.select(2), .width(32), .enable("false")) multiplexer_41 (
    .in0({32{1'b0}}), .in1(D30), .in2({32{1'b0}}), .in3(D30), .out(out_35), .sel({pause, playing}));
  not not_5 (not_5_out, swap_x_direction_right_wall);
  Comparator #(.width(5)) comparator_5 (.a(dmx_x_cord), .b(5'b11101), .eq(comparator_5_eq));  // open: gt, lt
  not not_6 (not_6_out, swap_x_direction_left_wall);
  Comparator #(.width(5)) comparator_6 (.a(dmx_x_cord), .b({5{1'b0}}), .eq(comparator_6_eq));  // open: gt, lt
  Comparator #(.width(5)) comparator_7 (.a(dmx_x_cord), .b(5'b11101), .eq(comparator_7_eq));  // open: gt, lt
  not not_7 (not_7_out, swap_x_direction_right_wall);
  Comparator #(.width(5)) comparator_8 (.a(dmx_x_cord), .b({5{1'b0}}), .eq(comparator_8_eq));  // open: gt, lt
  not not_8 (not_8_out, swap_x_direction_left_wall);
  Comparator #(.mode("unsigned")) comparator_9 (.a(p1_score_bin), .b(8'h8), .eq(win));  // open: gt, lt
  Comparator #(.mode("unsigned")) comparator_10 (.a(8'h8), .b(p2_score_bin), .eq(comparator_10_eq));  // open: gt, lt
  comp_y_cord comp_y_cord_1 (.in_1(racket2), .in_2(cord2), .\шарик (isDown), .out_4(r2));
  comp_y_cord comp_y_cord_2 (.in_1(player1), .in_2(cord1), .\шарик (isDown), .out_4(r1));
  and and_1 (and_1_out, not_5_out, comparator_5_eq);
  and and_2 (and_2_out, not_6_out, comparator_6_eq);
  Transistor #(.\type ("n")) transistor_1 (.in(not_7_out), .out(transistor_1_out), .gate(comparator_7_eq));
  Pull_Resistor pull_resistor_1 (.node(transistor_1_out));
  Pull_Resistor pull_resistor_2 (.node(pull_resistor_2_node));
  Transistor #(.\type ("n")) transistor_2 (.in(not_8_out), .out(pull_resistor_2_node), .gate(comparator_8_eq));
  or or_16 (gameover, win, comparator_10_eq);
  Multiplexer #(.select(2), .width(32), .enable("false")) multiplexer_42 (
    .in0({32{1'b0}}), .in1(D3), .in2({32{1'b0}}), .in3(D3), .out(out_8), .sel({pause, playing}));
  Multiplexer #(.select(2), .width(32), .enable("false")) multiplexer_43 (
    .in0(32'h602600), .in1(D7), .in2(lw7), .in3(D7), .out(out_12), .sel({pause, playing}));
  Multiplexer #(.select(2), .width(32), .enable("false")) multiplexer_44 (
    .in0(32'h904800), .in1(D11), .in2(lw11), .in3(D11), .out(out_16), .sel({pause, playing}));
  Multiplexer #(.select(2), .width(32), .enable("false")) multiplexer_45 (
    .in0(32'h924400), .in1(D15), .in2(lw15), .in3(D15), .out(out_20), .sel({pause, playing}));
  Multiplexer #(.select(2), .width(32), .enable("false")) multiplexer_46 (
    .in0(32'h641c00), .in1(D19), .in2(lw12), .in3(D19), .out(out_24), .sel({pause, playing}));
  Multiplexer #(.select(2), .width(32), .enable("false")) multiplexer_47 (
    .in0({32{1'b0}}), .in1(D23), .in2(lw8), .in3(D23), .out(out_28), .sel({pause, playing}));
  Multiplexer #(.select(2), .width(32), .enable("false")) multiplexer_48 (
    .in0(32'h4c4900), .in1(cord2), .in2(lw4), .in3(cord2), .out(out_32), .sel({pause, playing}));
  Multiplexer #(.select(2), .width(32), .enable("false")) multiplexer_49 (
    .in0({32{1'b0}}), .in1(D31), .in2({32{1'b0}}), .in3(D31), .out(out_36), .sel({pause, playing}));
  or or_17 (swap_x_direction_right_wall, r2, fail2);
  or or_18 (swap_x_direction_left_wall, r1, fail1);
  // OR_Gate or_19 has open pins: in0=and_1_out, in1=and_2_out, out=open
  or or_20 (lose, transistor_1_out, pull_resistor_2_node);
  comp_y_cord comp_y_cord_3 (.in_1(player1), .in_2(cord11), .\шарик (isDown), .out_4(swap_x_dir_left_r_to_left));
  comp_y_cord comp_y_cord_4 (.in_1(racket2), .in_2(cord22), .\шарик (isDown), .out_4(swap_x_dir_right_r_to_right));
  last_button_press last_button_press_1 (
    .button(w_button), .opposite_button(s_button), .button_pressed(w_pressed), .power(keyboard_power));
  last_button_press last_button_press_2 (
    .button(s_button), .opposite_button(w_button), .button_pressed(s_pressed), .power(keyboard_power));
  last_button_press last_button_press_3 (
    .button(o_button), .opposite_button(l_button), .button_pressed(o_pressed), .power(keyboard_power));
  last_button_press last_button_press_4 (
    .button(l_button), .opposite_button(o_button), .button_pressed(l_pressed), .power(keyboard_power));
  Shifter #(.width(32)) shifter_3 (.in({1'b0, decoder_2_out0, 1'b0}), .\dist (5'b00001), .out(shifter_3_out));
  Shifter #(.width(32), .shift("lr")) shifter_4 (
    .in({1'b0, decoder_2_out0, 1'b0}), .\dist (5'b00001), .out(shifter_4_out));
  Shifter #(.width(32)) shifter_5 (.in({1'b0, decoder_3_out0, 1'b0}), .\dist (5'b00001), .out(shifter_5_out));
  Shifter #(.width(32), .shift("lr")) shifter_6 (
    .in({1'b0, decoder_3_out0, 1'b0}), .\dist (5'b00001), .out(shifter_6_out));
  assign player1 = shifter_3_out | {1'b0, decoder_2_out0, 1'b0} | shifter_4_out;  // OR_Gate or_21, 32 bits wide
  assign player2 = shifter_5_out | {1'b0, decoder_3_out0, 1'b0} | shifter_6_out;  // OR_Gate or_22, 32 bits wide
  // Probe on dmx_x_cord
  Counter #(.ongoal("continue")) counter_5 (
    .Q(p2_score_bin), .clk(fail1), .clr(restart));  // open: load, D, count, carry
  Counter #(.ongoal("continue")) counter_6 (
    .Q(p1_score_bin), .clk(fail2), .clr(restart));  // open: load, D, count, carry
  Clock clock_1 (.out(keyboard_power));
  Pull_Resistor pull_resistor_3 (.node(is_ball_16));
  pause pause_1 (._14_y(D13), ._15_y(D14), ._13_y(D15), ._16_y(D16), ._18_y(D17), ._17_y(D18), .is_0_up(is_ball_16));
  // Probe on y_pause_cord
  Multiplexer #(.width(32)) multiplexer_50 (
    .in0(32'h1e), .in1(32'h78000000), .out(y_pause_cord), .sel(is_ball_16));  // open: en
  last_button_press last_button_press_5 (
    .button(space_pr), .opposite_button(l_button), .button_pressed(space_pressed), .power(keyboard_power));
  last_button_press last_button_press_6 (
    .button(restart), .opposite_button(l_button), .button_pressed(rest_pressed), .power(keyboard_power));
  nor nor_1 (fail1, dmx_x_cord[0], dmx_x_cord[1], dmx_x_cord[2], dmx_x_cord[3], dmx_x_cord[4]);
  and and_3 (fail2, dmx_x_cord[0], dmx_x_cord[1], dmx_x_cord[2], dmx_x_cord[3], dmx_x_cord[4]);
  bcd bcd_1 (._8bit_Input(p2_score_bin), .BCD_Output({out_37, out_38, out_39}));
  bcd bcd_2 (._8bit_Input(p1_score_bin), .BCD_Output({out_2, out_3, out_4}));
  Multiplexer #(.width(8)) multiplexer_51 (
    .in0(8'h5), .in1({8{1'b0}}), .out(multiplexer_51_out), .sel(pause));  // open: en
  frequency_divider frequency_divider_3 (.IN(transistor_3_out), .OUT(power), .n(multiplexer_51_out));  // open: _0
  Transistor #(.\type ("n")) transistor_3 (.in(keyboard_power), .out(transistor_3_out), .gate(playing));
  // Probe on keyboard_t
  // Probe on keyboard_t
  // Probe on keyboard_t
  Comparator #(.width(7)) comparator_11 (.a(keyboard_t), .b(7'b0100000), .eq(space_pr));  // open: gt, lt
  Comparator #(.width(7)) comparator_12 (.a(keyboard_t), .b(7'b1110000), .eq(comparator_12_eq));  // open: gt, lt
  Comparator #(.width(7)) comparator_13 (.a(keyboard_t), .b(7'b1110010), .eq(restart));  // open: gt, lt
  D_Flip_Flop d_ff_3 (.clk(space_pr), .D(space_pr), .Q(d_ff_3_q), .reset(restart));  // open: Qn, preset, en
  T_Flip_Flop t_ff_1 (.clk(comparator_12_eq), .T(comparator_12_eq), .Q(t_ff_1_q));  // open: Qn, preset, reset, en
  Comparator #(.width(5)) comparator_14 (.a(dmx_x_cord), .b(5'b00100), .eq(comparator_14_eq));  // open: gt, lt
  Comparator #(.width(5)) comparator_15 (.a(dmx_x_cord), .b(5'b00100), .eq(comparator_15_eq));  // open: gt, lt
  Comparator #(.width(5)) comparator_16 (.a(dmx_x_cord), .b(5'b11011), .eq(comparator_16_eq));  // open: gt, lt
  Comparator #(.width(5)) comparator_17 (.a(dmx_x_cord), .b(5'b11101), .eq(comparator_17_eq));  // open: gt, lt
  Comparator #(.width(5)) comparator_18 (.a(dmx_x_cord), .b(5'b00100), .eq(comparator_18_eq));  // open: gt, lt
  Comparator #(.width(5)) comparator_19 (.a(dmx_x_cord), .b(5'b00100), .eq(comparator_19_eq));  // open: gt, lt
  Comparator #(.width(5)) comparator_20 (.a(dmx_x_cord), .b(5'b11011), .eq(comparator_20_eq));  // open: gt, lt
  Comparator #(.width(5)) comparator_21 (.a(dmx_x_cord), .b(5'b11011), .eq(comparator_21_eq));  // open: gt, lt
  not not_9 (not_9_out, gameover);
  and and_4 (playing, not_9_out, d_ff_3_q);
  or or_23 (pause, t_ff_1_q, gameover);
  // Probe on keyboard_t
  Comparator #(.width(7)) comparator_22 (.a(keyboard_t), .b(7'b1100010), .eq(comparator_22_eq));  // open: gt, lt
  not not_10 (not_10_out, isDown);
  not not_11 (not_11_out, isLeft);
  not not_12 (not_12_out, isDown);
  not not_13 (not_13_out, isLeft);
  not not_14 (not_14_out, isDown);
  not not_15 (not_15_out, isDown);
  not not_16 (not_16_out, isLeft);
  not not_17 (not_17_out, isLeft);
  T_Flip_Flop t_ff_2 (.clk(comparator_22_eq), .T(comparator_22_eq), .Q(bot_enabled));  // open: Qn, preset, reset, en
  and and_5 (and_5_out, r1, isDown, w_pressed, comparator_14_eq, isLeft);
  and and_6 (and_6_out, r1, not_10_out, s_pressed, comparator_15_eq, isLeft);
  and and_7 (and_7_out, r2, isDown, o_pressed, comparator_16_eq, not_11_out);
  and and_8 (and_8_out, r2, not_12_out, l_pressed, comparator_17_eq, not_13_out);
  and and_9 (and_9_out, r1, not_14_out, w_pressed, comparator_18_eq, isLeft);
  and and_10 (and_10_out, r1, isDown, s_pressed, comparator_19_eq, isLeft);
  and and_11 (and_11_out, r2, not_15_out, o_pressed, comparator_20_eq, not_16_out);
  and and_12 (and_12_out, r2, isDown, l_pressed, comparator_21_eq, not_17_out);
  assign keyboard_t = test_keyboard | Keyboard;  // OR_Gate or_24, 7 bits wide
  or or_25 (or_25_out, and_5_out, and_6_out, and_7_out, and_8_out);
  or or_26 (P, and_9_out, and_10_out, and_11_out, and_12_out);
  or or_27 (or_27_out, or_25_out, P);
  not not_18 (not_18_out, P);
  not not_19 (not_19_out, restart);
  Counter #(.width(3), .max('h5), .ongoal("stay")) counter_7 (
    .load(not_18_out), .D(3'b011), .count(not_19_out), .Q(aoa), .clk(or_28_out));  // open: carry, clr
  or or_28 (or_28_out, restart, or_27_out);
  // Probe on aoa
  stopWatch2hz stopwatch2hz_1 (
    .start(playing), .takt(keyboard_power), .min_1(min_1), .min_0(min_0), .sec_1(sec_1), .sec_0(sec_0));
  Hex_Digit_Display hex_digit_display_1 (.value(out_2));  // open: dp
  Hex_Digit_Display hex_digit_display_2 (.value(out_3));  // open: dp
  Hex_Digit_Display hex_digit_display_3 (.value(out_4));  // open: dp
  DotMatrix #(.matrixcols(32), .matrixrows(32)) dotmatrix_1 (
    .col0(out_5), .col1(out_6), .col2(out_7), .col3(out_8), .col4(out_9), .col5(out_10), .col6(out_11),
    .col7(out_12), .col8(out_13), .col9(out_14), .col10(out_15), .col11(out_16), .col12(out_17),
    .col13(out_18), .col14(out_19), .col15(out_20), .col16(out_21), .col17(out_22), .col18(out_23),
    .col19(out_24), .col20(out_25), .col21(out_26), .col22(out_27), .col23(out_28), .col24(out_29),
    .col25(out_30), .col26(out_31), .col27(out_32), .col28(out_33), .col29(out_34), .col30(out_35),
    .col31(out_36));
  Hex_Digit_Display hex_digit_display_4 (.value(stopwatch2hz_2_min_1));  // open: dp
  Keyboard #(.buflen(1)) keyboard_1 (.clk(keyboard_power), .data(test_keyboard));  // open: re, clr, avail
  Hex_Digit_Display hex_digit_display_5 (.value(stopwatch2hz_2_sec_1));  // open: dp
  Hex_Digit_Display hex_digit_display_6 (.value(stopwatch2hz_2_min_0));  // open: dp
  stopWatch2hz stopwatch2hz_2 (
    .start(playing), .takt(keyboard_power), .min_1(stopwatch2hz_2_min_1), .min_0(stopwatch2hz_2_min_0),
    .sec_1(stopwatch2hz_2_sec_1), .sec_0(stopwatch2hz_2_sec_0));
  Hex_Digit_Display hex_digit_display_7 (.value(stopwatch2hz_2_sec_0));  // open: dp
  Hex_Digit_Display hex_digit_display_8 (.value(out_37));  // open: dp
  Hex_Digit_Display hex_digit_display_9 (.value(out_38));  // open: dp
  Hex_Digit_Display hex_digit_display_10 (.value(out_39));  // open: dp
  assign bit_extender_1_out = {{1{1'b0}}, aoa};  // Bit_Extender bit_extender_1
  Hex_Digit_Display hex_digit_display_11 (.value(bit_extender_1_out));  // open: dp

  // Other names for the same wires on the sheet: D4[31:0] = cord1; D27[31:0] = cord2; D2[31:0] = cord11;
  //   D29[31:0] = cord22; kpower = keyboard_power; n0[31:0] = out_5; n1[31:0] = out_6; n2[31:0] = out_7;
  //   n3[31:0] = out_8; n4[31:0] = out_9; n5[31:0] = out_10; n6[31:0] = out_11; n7[31:0] = out_12; n8[31:0] = out_13;
  //   n9[31:0] = out_14; n10[31:0] = out_15; n11[31:0] = out_16; n12[31:0] = out_17; n13[31:0] = out_18;
  //   n14[31:0] = out_19; n15[31:0] = out_20; n16[31:0] = out_21; n17[31:0] = out_22; n18[31:0] = out_23;
  //   n19[31:0] = out_24; n20[31:0] = out_25; n21[31:0] = out_26; n22[31:0] = out_27; n23[31:0] = out_28;
  //   n24[31:0] = out_29; n25[31:0] = out_30; n26[31:0] = out_31; n27[31:0] = out_32; n28[31:0] = out_33;
  //   n29[31:0] = out_34; n30[31:0] = out_35; n31[31:0] = out_36; p1_score[11:0] = {out_2, out_3, out_4};
  //   p2_score[11:0] = {out_37, out_38, out_39}; racket1[31:0] = player1; tunnel[1:0] = {pause, playing}

  // Notes on the sheet:
  //   win / lose screen
  //   PRESS SPACE
  //   PLAYER_1
  //   PLAYER_2
  //   BOT (Skynet in future)
  //   Playing scene
  //   Scene select
  //   00 - start scene
  //   01 - playing scene
  //   10 - gameover scene
  //   11 - pause scene
  //   Keyboard input
  //   Keyboard input
  //   движение по оси Y
  //   движение по оси X
  //   Gameover check
  //   если попадание: правая стенка
  //   если попадание: левая стенка
  //   неработающие варианты проверки на столкновение
  //   отскок между ракеткой и стенкой
  //   Запоминание последней кнопки
  //   Goal check
  //   Score count and print
  //   Power
  //   pause screen
  //   проверка на положение мяча
  //   запись координат паузы
  //   Keyboard input
  //   WARNING: я хз почему, но если передвигать этот чип - то логисим зависает
  //   уменьшение угла
  //   увеличение угла
  //   video out
  //   угол наклона мячика
  //   SCORE
  //   Player 1
  //   Inputs
  //   Player 1 - W and S
  //   Player 2 - O and L
  //   Pause - P
  //   Restart - R
  //   Bot - B
  //   Start game - SPACE
  //   Timer
  //   SCORE
  //   Player 2
endmodule

// ||
module comp_y_cord (
  input  [31:0] in_1,
  input  [31:0] in_2,
  input  \шарик ,
  output out_4
);

  wire or_1_out, or_2_out, or_3_out, or_4_out, or_5_out;
  wire [29:0] and_2_out, and_3_out;
  wire [31:0] and_1_out;

  assign and_1_out = in_1 & in_2;  // AND_Gate and_1, 32 bits wide
  assign and_2_out = in_1[30:1] & in_2[29:0];  // AND_Gate and_2, 30 bits wide
  or or_1 (or_1_out, and_1_out[0], and_1_out[1], and_1_out[2], and_1_out[3], and_1_out[4], and_1_out[5], and_1_out[6], and_1_out[7], and_1_out[8], and_1_out[9], and_1_out[10], and_1_out[11], and_1_out[12], and_1_out[13], and_1_out[14], and_1_out[15], and_1_out[17], and_1_out[18], and_1_out[19], and_1_out[20], and_1_out[21], and_1_out[22], and_1_out[23], and_1_out[24], and_1_out[25], and_1_out[26], and_1_out[27], and_1_out[28], and_1_out[29], and_1_out[30], and_1_out[31], and_1_out[16]);
  assign and_3_out = in_1[30:1] & in_2[31:2];  // AND_Gate and_3, 30 bits wide
  or or_2 (or_2_out, and_2_out[0], and_2_out[1], and_2_out[2], and_2_out[3], and_2_out[4], and_2_out[5], and_2_out[6], and_2_out[7], and_2_out[8], and_2_out[9], and_2_out[10], and_2_out[11], and_2_out[12], and_2_out[13], and_2_out[14], and_2_out[16], and_2_out[17], and_2_out[18], and_2_out[19], and_2_out[20], and_2_out[21], and_2_out[22], and_2_out[23], and_2_out[24], and_2_out[25], and_2_out[26], and_2_out[27], and_2_out[28], and_2_out[29], and_2_out[15]);
  or or_3 (or_3_out, and_3_out[0], and_3_out[1], and_3_out[2], and_3_out[3], and_3_out[4], and_3_out[5], and_3_out[6], and_3_out[7], and_3_out[8], and_3_out[9], and_3_out[10], and_3_out[11], and_3_out[12], and_3_out[13], and_3_out[14], and_3_out[16], and_3_out[17], and_3_out[18], and_3_out[19], and_3_out[20], and_3_out[21], and_3_out[22], and_3_out[23], and_3_out[24], and_3_out[25], and_3_out[26], and_3_out[27], and_3_out[28], and_3_out[29], and_3_out[15]);
  or or_4 (or_4_out, or_1_out, or_3_out);
  or or_5 (or_5_out, or_1_out, or_2_out);
  Multiplexer multiplexer_1 (.in0(or_5_out), .in1(or_4_out), .out(out_4), .sel(\шарик ));  // open: en

  // Other names for the same wires on the sheet: ball_cord_y[31:0] = in_2; rock_cord_y[31:0] = in_1;
  //   _1_down = \шарик 

  // Notes on the sheet:
  //   ракетка
  //   снизу вверх
  //   сверху вниз
endmodule

module parseScore (
  input  [7:0] in_1,
  output [3:0] out_2,
  output [3:0] out_3,
  output [3:0] out_4
);

  wire [7:0] divider_1_out, divider_2_out, multiplier_1_out, multiplier_2_out, subtractor_1_out,
       subtractor_2_out;

  // Probe on in_1
  // Probe on divider_1_out
  Divider divider_1 (.a(in_1), .b(8'ha), .out(divider_1_out));  // open: upper, rem
  Divider divider_2 (.a(divider_1_out), .b(8'ha), .out(divider_2_out));  // open: upper, rem
  Multiplier multiplier_1 (.a(divider_1_out), .b(8'ha), .out(multiplier_1_out));  // open: cin, cout
  // Probe on multiplier_1_out
  // Probe on multiplier_2_out
  Multiplier multiplier_2 (.a(divider_2_out), .b(8'ha), .out(multiplier_2_out));  // open: cin, cout
  Bit_Extender #(.out_width(4)) bit_extender_1 (.in(divider_2_out), .out(out_2));
  Subtractor subtractor_1 (.a(in_1), .b(multiplier_1_out), .out(subtractor_1_out));  // open: bin, bout
  // Probe on out_2
  // Probe on subtractor_2_out
  Subtractor subtractor_2 (.a(divider_1_out), .b(multiplier_2_out), .out(subtractor_2_out));  // open: bin, bout
  // Probe on subtractor_1_out
  Bit_Extender #(.out_width(4)) bit_extender_2 (.in(subtractor_2_out), .out(out_3));
  Bit_Extender #(.out_width(4)) bit_extender_3 (.in(subtractor_1_out), .out(out_4));

  // Notes on the sheet:
  //   OBSOLETE
  //   as of v0.1.3
endmodule

module frequency_divider (
  input  [7:0] n,
  input  IN,
  input  _0,
  output OUT
);

  wire comparator_1_eq, comparator_1_lt, or_1_out, or_2_out;
  wire [7:0] counter_1_q;

  Counter counter_1 (.count(IN), .Q(counter_1_q), .clk(IN), .clr(or_1_out));  // open: load, D, carry
  or or_1 (or_1_out, _0, or_2_out);
  Comparator #(.mode("unsigned")) comparator_1 (
    .a(n), .b(counter_1_q), .eq(comparator_1_eq), .lt(comparator_1_lt));  // open: gt
  or or_2 (or_2_out, comparator_1_eq, comparator_1_lt);
  T_Flip_Flop t_ff_1 (.clk(or_2_out), .T(or_2_out), .Q(OUT), .reset(_0));  // open: Qn, preset, en
endmodule

module bcd (
  input  [7:0] _8bit_Input,
  output [11:0] BCD_Output
);

  wire [3:0] bcd_helper_1_out, bcd_helper_2_out, bcd_helper_3_out, bcd_helper_4_out, bcd_helper_5_out,
       bcd_helper_6_out, bcd_helper_7_out, bcd_helper_8_out, bcd_helper_9_out, bcd_helper_10_out,
       bcd_helper_11_out, bcd_helper_12_out, bcd_helper_13_out, bcd_helper_14_out, bcd_helper_15_out,
       bcd_helper_16_out, bcd_helper_17_out, bcd_helper_18_out;
  wire [3:3] bcd_helper_21_out;

  // Probe on _8bit_Input
  bcd_helper bcd_helper_1 (.inp({3'b000, _8bit_Input[7]}), .out(bcd_helper_1_out));
  bcd_helper bcd_helper_2 (.inp(4'b0000), .out(bcd_helper_2_out));
  bcd_helper bcd_helper_3 (.inp(4'b0000), .out(bcd_helper_3_out));
  bcd_helper bcd_helper_4 (.inp({bcd_helper_1_out[2:0], _8bit_Input[6]}), .out(bcd_helper_4_out));
  bcd_helper bcd_helper_5 (.inp({bcd_helper_2_out[2:0], bcd_helper_1_out[3]}), .out(bcd_helper_5_out));
  bcd_helper bcd_helper_6 (.inp({bcd_helper_3_out[2:0], bcd_helper_2_out[3]}), .out(bcd_helper_6_out));
  bcd_helper bcd_helper_7 (.inp({bcd_helper_4_out[2:0], _8bit_Input[5]}), .out(bcd_helper_7_out));
  bcd_helper bcd_helper_8 (.inp({bcd_helper_5_out[2:0], bcd_helper_4_out[3]}), .out(bcd_helper_8_out));
  bcd_helper bcd_helper_9 (.inp({bcd_helper_6_out[2:0], bcd_helper_5_out[3]}), .out(bcd_helper_9_out));
  bcd_helper bcd_helper_10 (.inp({bcd_helper_7_out[2:0], _8bit_Input[4]}), .out(bcd_helper_10_out));
  bcd_helper bcd_helper_11 (.inp({bcd_helper_8_out[2:0], bcd_helper_7_out[3]}), .out(bcd_helper_11_out));
  bcd_helper bcd_helper_12 (.inp({bcd_helper_9_out[2:0], bcd_helper_8_out[3]}), .out(bcd_helper_12_out));
  bcd_helper bcd_helper_13 (.inp({bcd_helper_10_out[2:0], _8bit_Input[3]}), .out(bcd_helper_13_out));
  bcd_helper bcd_helper_14 (.inp({bcd_helper_11_out[2:0], bcd_helper_10_out[3]}), .out(bcd_helper_14_out));
  bcd_helper bcd_helper_15 (.inp({bcd_helper_12_out[2:0], bcd_helper_11_out[3]}), .out(bcd_helper_15_out));
  bcd_helper bcd_helper_16 (.inp({bcd_helper_13_out[2:0], _8bit_Input[2]}), .out(bcd_helper_16_out));
  bcd_helper bcd_helper_17 (.inp({bcd_helper_14_out[2:0], bcd_helper_13_out[3]}), .out(bcd_helper_17_out));
  bcd_helper bcd_helper_18 (.inp({bcd_helper_15_out[2:0], bcd_helper_14_out[3]}), .out(bcd_helper_18_out));
  bcd_helper bcd_helper_19 (.inp({bcd_helper_16_out[2:0], _8bit_Input[1]}), .out(BCD_Output[4:1]));
  bcd_helper bcd_helper_20 (.inp({bcd_helper_17_out[2:0], bcd_helper_16_out[3]}), .out(BCD_Output[8:5]));
  bcd_helper bcd_helper_21 (
    .inp({bcd_helper_18_out[2:0], bcd_helper_17_out[3]}), .out({bcd_helper_21_out[3], BCD_Output[11:9]}));
  // Probe on BCD_Output[11:8]
  // Probe on BCD_Output[7:4]
  // Probe on {BCD_Output[3:1], _8bit_Input[0]}

  assign BCD_Output[0] = _8bit_Input[0];

  // Notes on the sheet:
  //   The double dable algorithm
endmodule

module bcd_helper (
  input  [3:0] inp,
  output [3:0] out
);

  wire comparator_1_eq, comparator_1_lt, or_1_out;
  wire [3:0] adder_1_out;

  // Probe on inp
  Adder #(.width(4)) adder_1 (.a(4'b0011), .b(inp), .out(adder_1_out));  // open: cin, cout
  Comparator #(.width(4), .mode("unsigned")) comparator_1 (
    .a(4'b0101), .b(inp), .eq(comparator_1_eq), .lt(comparator_1_lt));  // open: gt
  or or_1 (or_1_out, comparator_1_eq, comparator_1_lt);
  Multiplexer #(.width(4)) multiplexer_1 (.in0(inp), .in1(adder_1_out), .out(out), .sel(or_1_out));  // open: en
endmodule

module pause (
  input  [31:0] _14_y,
  input  [31:0] _15_y,
  input  [31:0] _13_y,
  input  [31:0] _16_y,
  input  [31:0] _18_y,
  input  [31:0] _17_y,
  output is_0_up
);

  wire not_1_out, not_2_out, not_3_out, not_4_out, not_5_out, not_6_out, y_down_13, y_down_14, y_down_15,
       y_down_16, y_down_17, y_down_18, y_up_13, y_up_14, y_up_15, y_up_16, y_up_17, y_up_18;

  or or_1 (y_down_14, _14_y[0], _14_y[1], _14_y[2], _14_y[3], _14_y[4], _14_y[5], _14_y[6], _14_y[7], _14_y[8], _14_y[9], _14_y[10], _14_y[11], _14_y[12], _14_y[13], _14_y[14], _14_y[15]);
  or or_2 (y_up_14, _14_y[16], _14_y[17], _14_y[18], _14_y[19], _14_y[20], _14_y[21], _14_y[22], _14_y[23], _14_y[24], _14_y[25], _14_y[26], _14_y[27], _14_y[28], _14_y[29], _14_y[30], _14_y[31]);
  or or_3 (y_down_15, _15_y[0], _15_y[1], _15_y[2], _15_y[3], _15_y[4], _15_y[5], _15_y[6], _15_y[7], _15_y[8], _15_y[9], _15_y[10], _15_y[11], _15_y[12], _15_y[13], _15_y[14], _15_y[15]);
  or or_4 (y_up_15, _15_y[16], _15_y[17], _15_y[18], _15_y[19], _15_y[20], _15_y[21], _15_y[22], _15_y[23], _15_y[24], _15_y[25], _15_y[26], _15_y[27], _15_y[28], _15_y[29], _15_y[30], _15_y[31]);
  or or_5 (y_down_16, _16_y[0], _16_y[1], _16_y[2], _16_y[3], _16_y[4], _16_y[5], _16_y[6], _16_y[7], _16_y[8], _16_y[9], _16_y[10], _16_y[11], _16_y[12], _16_y[13], _16_y[14], _16_y[15]);
  or or_6 (y_up_16, _16_y[16], _16_y[17], _16_y[18], _16_y[19], _16_y[20], _16_y[21], _16_y[22], _16_y[23], _16_y[24], _16_y[25], _16_y[26], _16_y[27], _16_y[28], _16_y[29], _16_y[30], _16_y[31]);
  or or_7 (y_down_17, _17_y[0], _17_y[1], _17_y[2], _17_y[3], _17_y[4], _17_y[5], _17_y[6], _17_y[7], _17_y[8], _17_y[9], _17_y[10], _17_y[11], _17_y[12], _17_y[13], _17_y[14], _17_y[15]);
  or or_8 (y_up_17, _17_y[16], _17_y[17], _17_y[18], _17_y[19], _17_y[20], _17_y[21], _17_y[22], _17_y[23], _17_y[24], _17_y[25], _17_y[26], _17_y[27], _17_y[28], _17_y[29], _17_y[30], _17_y[31]);
  not not_1 (not_1_out, y_up_13);
  not not_2 (not_2_out, y_up_15);
  not not_3 (not_3_out, y_up_16);
  not not_4 (not_4_out, y_up_18);
  not not_5 (not_5_out, y_up_14);
  not not_6 (not_6_out, y_up_17);
  and and_1 (is_0_up, not_1_out, not_5_out, not_2_out, not_3_out, not_6_out, not_4_out);
  or or_9 (y_down_13, _13_y[0], _13_y[1], _13_y[2], _13_y[3], _13_y[4], _13_y[5], _13_y[6], _13_y[7], _13_y[8], _13_y[9], _13_y[10], _13_y[11], _13_y[12], _13_y[13], _13_y[14], _13_y[15]);
  or or_10 (y_up_13, _13_y[16], _13_y[17], _13_y[18], _13_y[19], _13_y[20], _13_y[21], _13_y[22], _13_y[23], _13_y[24], _13_y[25], _13_y[26], _13_y[27], _13_y[28], _13_y[29], _13_y[30], _13_y[31]);
  or or_11 (y_down_18, _18_y[0], _18_y[1], _18_y[2], _18_y[3], _18_y[4], _18_y[5], _18_y[6], _18_y[7], _18_y[8], _18_y[9], _18_y[10], _18_y[11], _18_y[12], _18_y[13], _18_y[14], _18_y[15]);
  or or_12 (y_up_18, _18_y[16], _18_y[17], _18_y[18], _18_y[19], _18_y[20], _18_y[21], _18_y[22], _18_y[23], _18_y[24], _18_y[25], _18_y[26], _18_y[27], _18_y[28], _18_y[29], _18_y[30], _18_y[31]);

  // Notes on the sheet:
  //   можно ставить сверху
endmodule

module start_screen (
);

  DotMatrix #(.matrixcols(32), .matrixrows(32)) dotmatrix_1 (
    .col0({32{1'b0}}), .col1({32{1'b0}}), .col2({32{1'b0}}), .col3({32{1'b0}}), .col4(32'hfe3200),
    .col5(32'h904900), .col6(32'h904900), .col7(32'h602600), .col8({32{1'b0}}), .col9(32'hfe7f00),
    .col10(32'h904800), .col11(32'h904800), .col12(32'h6e3000), .col13({32{1'b0}}), .col14(32'hfe3f00),
    .col15(32'h924400), .col16(32'h924400), .col17(32'h923f00), .col18({32{1'b0}}), .col19(32'h641c00),
    .col20(32'h922200), .col21(32'h924100), .col22(32'h4c4100), .col23({32{1'b0}}), .col24(32'h647f00),
    .col25(32'h924900), .col26(32'h924900), .col27(32'h4c4900), .col28({32{1'b0}}), .col29({32{1'b0}}),
    .col30({32{1'b0}}), .col31({32{1'b0}}));
  // Probe on nothing
endmodule

module parse_output (
);

  wire d_ff_1_q, d_ff_2_q, isDown, power, register_2_q, register_4_q;
  wire [4:0] bit_extender_2_out, counter_1_q, dmx_x_cord;
  wire [7:0] adder_1_out, adder_2_out, divider_1_out, divider_2_out, multiplexer_1_out, multiplexer_2_out,
       multiplexer_3_out, multiplexer_4_out, register_1_q, register_3_q, subtractor_1_out, subtractor_2_out;
  wire [31:0] decoder_1_out0, decoder_3_out0, demultiplexer_1_out0, demultiplexer_1_out1,
       demultiplexer_1_out2, demultiplexer_1_out3, demultiplexer_1_out4, demultiplexer_1_out5,
       demultiplexer_1_out6, demultiplexer_1_out7, demultiplexer_1_out8, demultiplexer_1_out9,
       demultiplexer_1_out10, demultiplexer_1_out11, demultiplexer_1_out12, demultiplexer_1_out13,
       demultiplexer_1_out14, demultiplexer_1_out15, demultiplexer_1_out16, demultiplexer_1_out17,
       demultiplexer_1_out18, demultiplexer_1_out19, demultiplexer_1_out20, demultiplexer_1_out21,
       demultiplexer_1_out22, demultiplexer_1_out23, demultiplexer_1_out24, demultiplexer_1_out25,
       demultiplexer_1_out26, demultiplexer_1_out27, demultiplexer_1_out28, demultiplexer_1_out29,
       demultiplexer_1_out30, demultiplexer_1_out31, dmx_y_cord;

  Clock clock_1 (.out(power));
  D_Flip_Flop d_ff_1 (.Q(d_ff_1_q), .preset(decoder_1_out0[31]), .reset(decoder_1_out0[0]));  // open: clk, D, Qn, en
  Register register_1 (.D(multiplexer_2_out), .Q(register_1_q), .clk(power));  // open: en, clr
  DotMatrix #(.matrixcols(32), .matrixrows(32)) dotmatrix_1 (
    .col0(demultiplexer_1_out0), .col1(demultiplexer_1_out1), .col2(demultiplexer_1_out2),
    .col3(demultiplexer_1_out3), .col4(demultiplexer_1_out4), .col5(demultiplexer_1_out5),
    .col6(demultiplexer_1_out6), .col7(demultiplexer_1_out7), .col8(demultiplexer_1_out8),
    .col9(demultiplexer_1_out9), .col10(demultiplexer_1_out10), .col11(demultiplexer_1_out11),
    .col12(demultiplexer_1_out12), .col13(demultiplexer_1_out13), .col14(demultiplexer_1_out14),
    .col15(demultiplexer_1_out15), .col16(demultiplexer_1_out16), .col17(demultiplexer_1_out17),
    .col18(demultiplexer_1_out18), .col19(demultiplexer_1_out19), .col20(demultiplexer_1_out20),
    .col21(demultiplexer_1_out21), .col22(demultiplexer_1_out22), .col23(demultiplexer_1_out23),
    .col24(demultiplexer_1_out24), .col25(demultiplexer_1_out25), .col26(demultiplexer_1_out26),
    .col27(demultiplexer_1_out27), .col28(demultiplexer_1_out28), .col29(demultiplexer_1_out29),
    .col30(demultiplexer_1_out30), .col31(demultiplexer_1_out31));
  Multiplexer #(.select(3), .width(8)) multiplexer_1 (
    .in0(8'h1), .in1(8'h2), .in2(8'h4), .in3(8'h4), .in4(8'h8), .out(multiplexer_1_out), .sel(3'b000));  // open: in5, in6, in7, en
  Demultiplexer #(.select(5), .width(32)) demultiplexer_1 (
    .out0(demultiplexer_1_out0), .out1(demultiplexer_1_out1), .out2(demultiplexer_1_out2),
    .out3(demultiplexer_1_out3), .out4(demultiplexer_1_out4), .out5(demultiplexer_1_out5),
    .out6(demultiplexer_1_out6), .out7(demultiplexer_1_out7), .out8(demultiplexer_1_out8),
    .out9(demultiplexer_1_out9), .out10(demultiplexer_1_out10), .out11(demultiplexer_1_out11),
    .out12(demultiplexer_1_out12), .out13(demultiplexer_1_out13), .out14(demultiplexer_1_out14),
    .out15(demultiplexer_1_out15), .out16(demultiplexer_1_out16), .out17(demultiplexer_1_out17),
    .out18(demultiplexer_1_out18), .out19(demultiplexer_1_out19), .out20(demultiplexer_1_out20),
    .out21(demultiplexer_1_out21), .out22(demultiplexer_1_out22), .out23(demultiplexer_1_out23),
    .out24(demultiplexer_1_out24), .out25(demultiplexer_1_out25), .out26(demultiplexer_1_out26),
    .out27(demultiplexer_1_out27), .out28(demultiplexer_1_out28), .out29(demultiplexer_1_out29),
    .out30(demultiplexer_1_out30), .out31(demultiplexer_1_out31), .in(dmx_y_cord), .sel(dmx_x_cord));  // open: en
  Adder adder_1 (.a(register_1_q), .b(multiplexer_1_out), .out(adder_1_out));  // open: cin, cout
  Subtractor subtractor_1 (.a(register_1_q), .b(multiplexer_1_out), .out(subtractor_1_out));  // open: bin, bout
  Multiplexer #(.width(8)) multiplexer_2 (
    .in0(adder_1_out), .in1(subtractor_1_out), .out(multiplexer_2_out), .sel(register_2_q));  // open: en
  Register #(.width(1)) register_2 (.D(d_ff_1_q), .Q(register_2_q), .clk(power));  // open: en, clr
  Divider divider_1 (.a(multiplexer_2_out), .b(8'h8), .out(divider_1_out));  // open: upper, rem
  Bit_Extender #(.out_width(5)) bit_extender_1 (.in(divider_1_out), .out(dmx_x_cord));
  D_Flip_Flop d_ff_2 (.Q(d_ff_2_q), .preset(dmx_y_cord[31]), .reset(dmx_y_cord[0]));  // open: clk, D, Qn, en
  Decoder #(.select(5)) decoder_1 (
    .out0(decoder_1_out0[0]), .out1(decoder_1_out0[1]), .out2(decoder_1_out0[2]), .out3(decoder_1_out0[3]),
    .out4(decoder_1_out0[4]), .out5(decoder_1_out0[5]), .out6(decoder_1_out0[6]), .out7(decoder_1_out0[7]),
    .out8(decoder_1_out0[8]), .out9(decoder_1_out0[9]), .out10(decoder_1_out0[10]),
    .out11(decoder_1_out0[11]), .out12(decoder_1_out0[12]), .out13(decoder_1_out0[13]),
    .out14(decoder_1_out0[14]), .out15(decoder_1_out0[15]), .out16(decoder_1_out0[16]),
    .out17(decoder_1_out0[17]), .out18(decoder_1_out0[18]), .out19(decoder_1_out0[19]),
    .out20(decoder_1_out0[20]), .out21(decoder_1_out0[21]), .out22(decoder_1_out0[22]),
    .out23(decoder_1_out0[23]), .out24(decoder_1_out0[24]), .out25(decoder_1_out0[25]),
    .out26(decoder_1_out0[26]), .out27(decoder_1_out0[27]), .out28(decoder_1_out0[28]),
    .out29(decoder_1_out0[29]), .out30(decoder_1_out0[30]), .out31(decoder_1_out0[31]), .sel(dmx_x_cord));  // open: en
  Register register_3 (.D(multiplexer_4_out), .Q(register_3_q), .clk(power));  // open: en, clr
  Multiplexer #(.select(3), .width(8)) multiplexer_3 (
    .in0(8'h8), .in1(8'h4), .in2(8'h4), .in3(8'h2), .in4(8'h1), .out(multiplexer_3_out), .sel(3'b000));  // open: in5, in6, in7, en
  Subtractor subtractor_2 (.a(register_3_q), .b(multiplexer_3_out), .out(subtractor_2_out));  // open: bin, bout
  Adder adder_2 (.a(register_3_q), .b(multiplexer_3_out), .out(adder_2_out));  // open: cin, cout
  Multiplexer #(.width(8)) multiplexer_4 (
    .in0(adder_2_out), .in1(subtractor_2_out), .out(multiplexer_4_out), .sel(register_4_q));  // open: en
  Register #(.width(1)) register_4 (.D(d_ff_2_q), .Q(register_4_q), .clk(power));  // open: en, clr
  Divider divider_2 (.a(multiplexer_4_out), .b(8'h8), .out(divider_2_out));  // open: upper, rem
  Bit_Extender #(.out_width(5)) bit_extender_2 (.in(divider_2_out), .out(bit_extender_2_out));
  Decoder #(.select(5)) decoder_2 (
    .out0(dmx_y_cord[0]), .out1(dmx_y_cord[1]), .out2(dmx_y_cord[2]), .out3(dmx_y_cord[3]),
    .out4(dmx_y_cord[4]), .out5(dmx_y_cord[5]), .out6(dmx_y_cord[6]), .out7(dmx_y_cord[7]),
    .out8(dmx_y_cord[8]), .out9(dmx_y_cord[9]), .out10(dmx_y_cord[10]), .out11(dmx_y_cord[11]),
    .out12(dmx_y_cord[12]), .out13(dmx_y_cord[13]), .out14(dmx_y_cord[14]), .out15(dmx_y_cord[15]),
    .out16(dmx_y_cord[16]), .out17(dmx_y_cord[17]), .out18(dmx_y_cord[18]), .out19(dmx_y_cord[19]),
    .out20(dmx_y_cord[20]), .out21(dmx_y_cord[21]), .out22(dmx_y_cord[22]), .out23(dmx_y_cord[23]),
    .out24(dmx_y_cord[24]), .out25(dmx_y_cord[25]), .out26(dmx_y_cord[26]), .out27(dmx_y_cord[27]),
    .out28(dmx_y_cord[28]), .out29(dmx_y_cord[29]), .out30(dmx_y_cord[30]), .out31(dmx_y_cord[31]),
    .sel(bit_extender_2_out));  // open: en
  D_Flip_Flop d_ff_3 (.Q(isDown), .preset(decoder_3_out0[31]), .reset(decoder_3_out0[0]));  // open: clk, D, Qn, en
  Counter #(.width(5), .max('h1f)) counter_1 (
    .load(isDown), .Q(counter_1_q), .clk(power));  // open: D, count, carry, clr
  Decoder #(.select(5)) decoder_3 (
    .out0(decoder_3_out0[0]), .out1(decoder_3_out0[1]), .out2(decoder_3_out0[2]), .out3(decoder_3_out0[3]),
    .out4(decoder_3_out0[4]), .out5(decoder_3_out0[5]), .out6(decoder_3_out0[6]), .out7(decoder_3_out0[7]),
    .out8(decoder_3_out0[8]), .out9(decoder_3_out0[9]), .out10(decoder_3_out0[10]),
    .out11(decoder_3_out0[11]), .out12(decoder_3_out0[12]), .out13(decoder_3_out0[13]),
    .out14(decoder_3_out0[14]), .out15(decoder_3_out0[15]), .out16(decoder_3_out0[16]),
    .out17(decoder_3_out0[17]), .out18(decoder_3_out0[18]), .out19(decoder_3_out0[19]),
    .out20(decoder_3_out0[20]), .out21(decoder_3_out0[21]), .out22(decoder_3_out0[22]),
    .out23(decoder_3_out0[23]), .out24(decoder_3_out0[24]), .out25(decoder_3_out0[25]),
    .out26(decoder_3_out0[26]), .out27(decoder_3_out0[27]), .out28(decoder_3_out0[28]),
    .out29(decoder_3_out0[29]), .out30(decoder_3_out0[30]), .out31(decoder_3_out0[31]), .sel(counter_1_q));  // open: en

  // Notes on the sheet:
  //   движение по оси x
  //   движение по оси y
  //   движение по оси x
endmodule

module stopWatch2hz (
  input  start,
  input  takt,
  output [3:0] min_1,
  output [3:0] min_0,
  output [3:0] sec_1,
  output [3:0] sec_0
);

  wire and_1_out, and_2_out, and_3_out, and_4_out, and_5_out, d_ff_1_q, frequency_divider_1_out,
       frequency_divider_11bit_1_out, not_1_out, not_2_out, not_3_out, not_4_out, not_5_out, not_6_out;

  Counter #(.width(4), .max('hf)) counter_1 (.Q(min_1), .clk(and_1_out));  // open: load, D, count, carry, clr
  frequency_divider_11bit frequency_divider_11bit_1 (
    .IN(takt), .n(11'h390), .OUT(frequency_divider_11bit_1_out));  // open: _0
  // Probe on min_0
  Counter #(.width(4), .max('hf)) counter_2 (
    .Q(min_0), .clk(and_4_out), .clr(and_1_out));  // open: load, D, count, carry
  frequency_divider frequency_divider_1 (
    .IN(frequency_divider_11bit_1_out), .OUT(frequency_divider_1_out), .n(8'h2));  // open: _0
  D_Flip_Flop d_ff_1 (.Q(d_ff_1_q), .preset(frequency_divider_1_out));  // open: clk, D, Qn, en, reset
  not not_1 (not_1_out, min_0[0]);
  not not_2 (not_2_out, min_0[2]);
  and and_1 (and_1_out, not_1_out, min_0[1], not_2_out, min_0[3]);
  // Probe on sec_1
  Counter #(.width(4), .max('hf)) counter_3 (
    .Q(sec_1), .clk(and_5_out), .clr(and_4_out));  // open: load, D, count, carry
  and and_2 (and_2_out, start, d_ff_1_q);
  and and_3 (and_3_out, and_2_out, frequency_divider_11bit_1_out);
  Hex_Digit_Display hex_digit_display_1 (.value(min_1));  // open: dp
  Hex_Digit_Display hex_digit_display_2 (.value(min_0));  // open: dp
  not not_3 (not_3_out, sec_1[0]);
  not not_4 (not_4_out, sec_1[3]);
  Hex_Digit_Display hex_digit_display_3 (.value(sec_1));  // open: dp
  Counter #(.width(4), .max('hf)) counter_4 (
    .Q(sec_0), .clk(and_3_out), .clr(and_5_out));  // open: load, D, count, carry
  and and_4 (and_4_out, not_3_out, sec_1[1], sec_1[2], not_4_out);
  Hex_Digit_Display hex_digit_display_4 (.value(sec_0));  // open: dp
  // Probe on sec_0
  not not_5 (not_5_out, sec_0[0]);
  not not_6 (not_6_out, sec_0[2]);
  and and_5 (and_5_out, not_5_out, sec_0[1], not_6_out, sec_0[3]);
endmodule

module frequency_divider_11bit (
  input  [10:0] n,
  input  IN,
  input  _0,
  output OUT
);

  wire comparator_1_eq, comparator_1_lt, or_1_out, or_2_out;
  wire [10:0] counter_1_q;

  Counter #(.width(11), .max('h7ff)) counter_1 (
    .count(IN), .Q(counter_1_q), .clk(IN), .clr(or_1_out));  // open: load, D, carry
  or or_1 (or_1_out, _0, or_2_out);
  Comparator #(.width(11), .mode("unsigned")) comparator_1 (
    .a(n), .b(counter_1_q), .eq(comparator_1_eq), .lt(comparator_1_lt));  // open: gt
  or or_2 (or_2_out, comparator_1_eq, comparator_1_lt);
  T_Flip_Flop t_ff_1 (.clk(or_2_out), .T(or_2_out), .Q(OUT), .reset(_0));  // open: Qn, preset, en
endmodule

module PING_PONG (
);

  wire movepoint_1_keyboard_power;
  wire [3:0] movepoint_1_min_0, movepoint_1_min_1, movepoint_1_out_2, movepoint_1_out_3, movepoint_1_out_4,
       movepoint_1_out_37, movepoint_1_out_38, movepoint_1_out_39, movepoint_1_sec_0, movepoint_1_sec_1;
  wire [6:0] keyboard_1_data;
  wire [31:0] movepoint_1_out_5, movepoint_1_out_6, movepoint_1_out_7, movepoint_1_out_8, movepoint_1_out_9,
       movepoint_1_out_10, movepoint_1_out_11, movepoint_1_out_12, movepoint_1_out_13, movepoint_1_out_14,
       movepoint_1_out_15, movepoint_1_out_16, movepoint_1_out_17, movepoint_1_out_18, movepoint_1_out_19,
       movepoint_1_out_20, movepoint_1_out_21, movepoint_1_out_22, movepoint_1_out_23, movepoint_1_out_24,
       movepoint_1_out_25, movepoint_1_out_26, movepoint_1_out_27, movepoint_1_out_28, movepoint_1_out_29,
       movepoint_1_out_30, movepoint_1_out_31, movepoint_1_out_32, movepoint_1_out_33, movepoint_1_out_34,
       movepoint_1_out_35, movepoint_1_out_36;

  DotMatrix #(.matrixcols(32), .matrixrows(32)) dotmatrix_1 (
    .col0(movepoint_1_out_5), .col1(movepoint_1_out_6), .col2(movepoint_1_out_7), .col3(movepoint_1_out_8),
    .col4(movepoint_1_out_9), .col5(movepoint_1_out_10), .col6(movepoint_1_out_11),
    .col7(movepoint_1_out_12), .col8(movepoint_1_out_13), .col9(movepoint_1_out_14),
    .col10(movepoint_1_out_15), .col11(movepoint_1_out_16), .col12(movepoint_1_out_17),
    .col13(movepoint_1_out_18), .col14(movepoint_1_out_19), .col15(movepoint_1_out_20),
    .col16(movepoint_1_out_21), .col17(movepoint_1_out_22), .col18(movepoint_1_out_23),
    .col19(movepoint_1_out_24), .col20(movepoint_1_out_25), .col21(movepoint_1_out_26),
    .col22(movepoint_1_out_27), .col23(movepoint_1_out_28), .col24(movepoint_1_out_29),
    .col25(movepoint_1_out_30), .col26(movepoint_1_out_31), .col27(movepoint_1_out_32),
    .col28(movepoint_1_out_33), .col29(movepoint_1_out_34), .col30(movepoint_1_out_35),
    .col31(movepoint_1_out_36));
  movePoint movepoint_1 (
    .out_5(movepoint_1_out_5), .out_6(movepoint_1_out_6), .out_7(movepoint_1_out_7),
    .out_8(movepoint_1_out_8), .out_9(movepoint_1_out_9), .out_10(movepoint_1_out_10),
    .out_11(movepoint_1_out_11), .out_12(movepoint_1_out_12), .out_13(movepoint_1_out_13),
    .out_14(movepoint_1_out_14), .out_15(movepoint_1_out_15), .out_16(movepoint_1_out_16),
    .out_17(movepoint_1_out_17), .out_18(movepoint_1_out_18), .out_19(movepoint_1_out_19),
    .out_20(movepoint_1_out_20), .out_21(movepoint_1_out_21), .out_22(movepoint_1_out_22),
    .out_23(movepoint_1_out_23), .out_24(movepoint_1_out_24), .out_25(movepoint_1_out_25),
    .out_26(movepoint_1_out_26), .out_27(movepoint_1_out_27), .out_28(movepoint_1_out_28),
    .out_29(movepoint_1_out_29), .out_30(movepoint_1_out_30), .out_31(movepoint_1_out_31),
    .out_32(movepoint_1_out_32), .out_33(movepoint_1_out_33), .Keyboard(keyboard_1_data),
    .out_34(movepoint_1_out_34), .out_35(movepoint_1_out_35), .out_36(movepoint_1_out_36),
    .keyboard_power(movepoint_1_keyboard_power), .out_4(movepoint_1_out_4), .out_3(movepoint_1_out_3),
    .out_2(movepoint_1_out_2), .out_39(movepoint_1_out_39), .out_38(movepoint_1_out_38),
    .out_37(movepoint_1_out_37), .min_1(movepoint_1_min_1), .min_0(movepoint_1_min_0),
    .sec_1(movepoint_1_sec_1), .sec_0(movepoint_1_sec_0));
  Hex_Digit_Display hex_digit_display_1 (.value(movepoint_1_out_2));  // open: dp
  Hex_Digit_Display hex_digit_display_2 (.value(movepoint_1_out_4));  // open: dp
  Hex_Digit_Display hex_digit_display_3 (.value(movepoint_1_out_3));  // open: dp
  Hex_Digit_Display hex_digit_display_4 (.value(movepoint_1_min_0));  // open: dp
  Hex_Digit_Display hex_digit_display_5 (.value(movepoint_1_min_1));  // open: dp
  Keyboard keyboard_1 (.clk(movepoint_1_keyboard_power), .data(keyboard_1_data));  // open: re, clr, avail
  Hex_Digit_Display hex_digit_display_6 (.value(movepoint_1_sec_1));  // open: dp
  Hex_Digit_Display hex_digit_display_7 (.value(movepoint_1_sec_0));  // open: dp
  Hex_Digit_Display hex_digit_display_8 (.value(movepoint_1_out_38));  // open: dp
  Hex_Digit_Display hex_digit_display_9 (.value(movepoint_1_out_37));  // open: dp
  Hex_Digit_Display hex_digit_display_10 (.value(movepoint_1_out_39));  // open: dp

  // Notes on the sheet:
  //   SCORE
  //   Player 1
  //   Player 1 - W and S
  //   Player 2 - O and L
  //   Pause - P
  //   Restart - R
  //   Bot - B
  //   Start game - SPACE
  //   SCORE
  //   Player 2
endmodule

module bot_borris (
  input  [31:0] X,
  input  [31:0] Y,
  input  [31:0] Vx,
  input  [31:0] Vy,
  output [31:0] New_Y
);

  wire cdm_8_mark5_1_p9, cdm_8_mark5_1_p10, cdm_8_mark5_1_p12, cdm_8_mark5_1_p13, cdm_8_mark5_1_p14,
       cdm_8_mark5_1_p15, cdm_8_mark5_1_p16, cdm_8_mark5_1_p17, cdm_8_mark5_1_p18, cdm_8_mark5_1_p19, clk,
       decoder_1_out0, decoder_1_out1, IAck, IRQ, not_1_out;
  wire [2:0] vec;
  wire [7:0] cdm_8_mark5_1_p20, cdm_8_mark5_1_p21, cdm_8_mark5_1_p22, controlled_buffer_2_out;

  Clock clock_1 (.out(clk));
  // Probe on cdm_8_mark5_1_p9
  // Probe on cdm_8_mark5_1_p13
  // Probe on cdm_8_mark5_1_p12
  // Probe on cdm_8_mark5_1_p10
  // Probe on cdm_8_mark5_1_p14
  // Probe on cdm_8_mark5_1_p15
  // Probe on cdm_8_mark5_1_p16
  // CdM_8_mark5 cdm_8_mark5_1: pin names not known; wires that end beside it: X, Y, Vx, Vy, New_Y, IRQ, vec, IAck, cdm_8_mark5_1_p9, cdm_8_mark5_1_p10, clk, cdm_8_mark5_1_p12, cdm_8_mark5_1_p13, cdm_8_mark5_1_p14, cdm_8_mark5_1_p15, cdm_8_mark5_1_p16, cdm_8_mark5_1_p17, cdm_8_mark5_1_p18, cdm_8_mark5_1_p19, cdm_8_mark5_1_p20, cdm_8_mark5_1_p21, cdm_8_mark5_1_p22
  not not_1 (not_1_out, cdm_8_mark5_1_p19);
  assign cdm_8_mark5_1_p22 = cdm_8_mark5_1_p19 ? controlled_buffer_2_out : 8'bz;  // Controlled_Buffer controlled_buffer_1
  Decoder decoder_1 (.out0(decoder_1_out0), .out1(decoder_1_out1), .sel(cdm_8_mark5_1_p17), .en(cdm_8_mark5_1_p18));
  assign controlled_buffer_2_out = not_1_out ? cdm_8_mark5_1_p21 : 8'bz;  // Controlled_Buffer controlled_buffer_2
  ROM rom_1 (.addr(cdm_8_mark5_1_p20), .data(controlled_buffer_2_out), .sel(decoder_1_out0));
  RAM ram_1 (
    .addr(cdm_8_mark5_1_p20), .data(controlled_buffer_2_out), .sel(decoder_1_out1), .clk(clk),
    .ld(cdm_8_mark5_1_p19));  // open: clr

  // Notes on the sheet:
  //   D2 00  D0 2D B0  D1 2B B5  71 ED 11 85 14 85 8E EE 08 8E  D0 2E B0  D1 2C B5   8A E0 1E 14 EE 18 14   94 94 94 98 98 98  D1 2F A4  D0 2F D4  01 01 0A 1F  00
  //   contents of rom_1 (hex, n*v repeats v):
  //   d2 0 d0 2d b0 d1 2b b5 71 ed 11 85 14 85 8e ee 8 8e d0 2e b0 d1 2c b5 8a e0 1e 14 ee 18 14 94 94 94
  //   98 98 98 d1 2f a4 d0 2f d4 1 1 a 1f 195*0 1c
endmodule

module last_button_press (
  input  button,
  input  opposite_button,
  input  power,
  output button_pressed
);

  wire frequency_divider_1_out, or_1_out, or_2_out;

  frequency_divider frequency_divider_1 (.IN(power), .OUT(frequency_divider_1_out), .n({8{1'b1}}), ._0(or_1_out));
  or or_1 (or_1_out, button, frequency_divider_1_out);
  D_Flip_Flop d_ff_1 (.clk(button), .D(button), .Q(button_pressed), .reset(or_2_out));  // open: Qn, preset, en
  or or_2 (or_2_out, frequency_divider_1_out, opposite_button);
endmodule

module win_screen (
  input  in_1
);

  wire [31:0] multiplexer_1_out, multiplexer_2_out, multiplexer_3_out, multiplexer_4_out, multiplexer_5_out,
       multiplexer_6_out, multiplexer_7_out, multiplexer_8_out, multiplexer_9_out, multiplexer_10_out,
       multiplexer_11_out, multiplexer_12_out, multiplexer_13_out, multiplexer_14_out, multiplexer_15_out,
       multiplexer_16_out, multiplexer_17_out, multiplexer_18_out, multiplexer_19_out, multiplexer_20_out,
       multiplexer_21_out, multiplexer_22_out, multiplexer_23_out, multiplexer_24_out;

  DotMatrix #(.matrixcols(32), .matrixrows(32)) dotmatrix_1 (
    .col0({32{1'b0}}), .col1({32{1'b0}}), .col2({32{1'b0}}), .col3({32{1'b0}}), .col4(32'h60000),
    .col5(32'h90000), .col6(32'h9c000), .col7(32'h63000), .col8(32'h10c00), .col9(32'h10200),
    .col10(32'h8200), .col11(32'h8200), .col12(32'h4200), .col13(32'h18200), .col14(32'h360200),
    .col15(32'h480200), .col16(32'h480200), .col17(32'h360200), .col18(32'h18200), .col19(32'h4200),
    .col20(32'h8200), .col21(32'h8200), .col22(32'h10200), .col23(32'h10c00), .col24(32'h63000),
    .col25(32'h9c000), .col26(32'h90000), .col27(32'h60000), .col28({32{1'b0}}), .col29({32{1'b0}}),
    .col30({32{1'b0}}), .col31({32{1'b0}}));
  Multiplexer #(.width(32)) multiplexer_1 (
    .in0({32{1'b0}}), .in1(32'h60000), .out(multiplexer_1_out), .sel(in_1));  // open: en
  Multiplexer #(.width(32)) multiplexer_2 (
    .in0({32{1'b0}}), .in1(32'h90000), .out(multiplexer_2_out), .sel(in_1));  // open: en
  Multiplexer #(.width(32)) multiplexer_3 (
    .in0({32{1'b0}}), .in1(32'h9c000), .out(multiplexer_3_out), .sel(in_1));  // open: en
  Multiplexer #(.width(32)) multiplexer_4 (
    .in0({32{1'b0}}), .in1(32'h63000), .out(multiplexer_4_out), .sel(in_1));  // open: en
  Multiplexer #(.width(32)) multiplexer_5 (
    .in0(32'h7c000), .in1(32'h10c00), .out(multiplexer_5_out), .sel(in_1));  // open: en
  Multiplexer #(.width(32)) multiplexer_6 (
    .in0(32'h382000), .in1(32'h10200), .out(multiplexer_6_out), .sel(in_1));  // open: en
  Multiplexer #(.width(32)) multiplexer_7 (
    .in0(32'h439000), .in1(32'h8200), .out(multiplexer_7_out), .sel(in_1));  // open: en
  Multiplexer #(.width(32)) multiplexer_8 (
    .in0(32'h87d000), .in1(32'h8200), .out(multiplexer_8_out), .sel(in_1));  // open: en
  Multiplexer #(.width(32)) multiplexer_9 (
    .in0(32'h87cf00), .in1(32'h4200), .out(multiplexer_9_out), .sel(in_1));  // open: en
  Multiplexer #(.width(32)) multiplexer_10 (
    .in0(32'h107c080), .in1(32'h18200), .out(multiplexer_10_out), .sel(in_1));  // open: en
  Multiplexer #(.width(32)) multiplexer_11 (
    .in0(32'h1038080), .in1(32'h360200), .out(multiplexer_11_out), .sel(in_1));  // open: en
  Multiplexer #(.width(32)) multiplexer_12 (
    .in0(32'h1001880), .in1(32'h480200), .out(multiplexer_12_out), .sel(in_1));  // open: en
  Multiplexer #(.width(32)) multiplexer_13 (
    .in0(32'h1001880), .in1(32'h480200), .out(multiplexer_13_out), .sel(in_1));  // open: en
  Multiplexer #(.width(32)) multiplexer_14 (
    .in0(32'h1038080), .in1(32'h360200), .out(multiplexer_14_out), .sel(in_1));  // open: en
  Multiplexer #(.width(32)) multiplexer_15 (
    .in0(32'h107c080), .in1(32'h18200), .out(multiplexer_15_out));  // open: sel, en
  Multiplexer #(.width(32)) multiplexer_16 (
    .in0(32'h87cf00), .in1(32'h4200), .out(multiplexer_16_out), .sel(in_1));  // open: en
  Multiplexer #(.width(32)) multiplexer_17 (
    .in0(32'h87d000), .in1(32'h8200), .out(multiplexer_17_out), .sel(in_1));  // open: en
  Multiplexer #(.width(32)) multiplexer_18 (
    .in0(32'h439000), .in1(32'h8200), .out(multiplexer_18_out), .sel(in_1));  // open: en
  Multiplexer #(.width(32)) multiplexer_19 (
    .in0(32'h382000), .in1(32'h10200), .out(multiplexer_19_out), .sel(in_1));  // open: en
  Multiplexer #(.width(32)) multiplexer_20 (
    .in0(32'h7c000), .in1(32'h10c00), .out(multiplexer_20_out), .sel(in_1));  // open: en
  Multiplexer #(.width(32)) multiplexer_21 (
    .in0({32{1'b0}}), .in1(32'h63000), .out(multiplexer_21_out), .sel(in_1));  // open: en
  Multiplexer #(.width(32)) multiplexer_22 (
    .in0({32{1'b0}}), .in1(32'h9c000), .out(multiplexer_22_out), .sel(in_1));  // open: en
  Multiplexer #(.width(32)) multiplexer_23 (
    .in0({32{1'b0}}), .in1(32'h90000), .out(multiplexer_23_out), .sel(in_1));  // open: en
  Multiplexer #(.width(32)) multiplexer_24 (
    .in0({32{1'b0}}), .in1(32'h60000), .out(multiplexer_24_out), .sel(in_1));  // open: en
  DotMatrix #(.matrixcols(32), .matrixrows(32)) dotmatrix_2 (
    .col4(multiplexer_1_out), .col5(multiplexer_2_out), .col6(multiplexer_3_out), .col7(multiplexer_4_out),
    .col8(multiplexer_5_out), .col9(multiplexer_6_out), .col10(multiplexer_7_out), .col11(multiplexer_8_out),
    .col12(multiplexer_9_out), .col13(multiplexer_10_out), .col14(multiplexer_11_out),
    .col15(multiplexer_12_out), .col16(multiplexer_13_out), .col17(multiplexer_14_out),
    .col18(multiplexer_15_out), .col19(multiplexer_16_out), .col20(multiplexer_17_out),
    .col21(multiplexer_18_out), .col22(multiplexer_19_out), .col23(multiplexer_20_out),
    .col24(multiplexer_21_out), .col25(multiplexer_22_out), .col26(multiplexer_23_out),
    .col27(multiplexer_24_out));  // open: col0, col1, col2, col3, col28, col29, col30, col31
  DotMatrix #(.matrixcols(32), .matrixrows(32)) dotmatrix_3 (
    .col0({32{1'b0}}), .col1({32{1'b0}}), .col2({32{1'b0}}), .col3({32{1'b0}}), .col4({32{1'b0}}),
    .col5({32{1'b0}}), .col6({32{1'b0}}), .col7({32{1'b0}}), .col8(32'h7c000), .col9(32'h382000),
    .col10(32'h439000), .col11(32'h87d000), .col12(32'h87cf00), .col13(32'h107c080), .col14(32'h1038080),
    .col15(32'h1001880), .col16(32'h1001880), .col17(32'h1038080), .col18(32'h107c080), .col19(32'h87cf00),
    .col20(32'h87d000), .col21(32'h439000), .col22(32'h382000), .col23(32'h7c000), .col24({32{1'b0}}),
    .col25({32{1'b0}}), .col26({32{1'b0}}), .col27({32{1'b0}}), .col28({32{1'b0}}), .col29({32{1'b0}}),
    .col30({32{1'b0}}), .col31({32{1'b0}}));

  // Other names for the same wires on the sheet: win = in_1
endmodule

module lose_screen (
);

  DotMatrix #(.matrixcols(32), .matrixrows(32)) dotmatrix_1 (
    .col0({32{1'b0}}), .col1({32{1'b0}}), .col2({32{1'b0}}), .col3({32{1'b0}}), .col4({32{1'b0}}),
    .col5({32{1'b0}}), .col6({32{1'b0}}), .col7({32{1'b0}}), .col8(32'h7c000), .col9(32'h382000),
    .col10(32'h439000), .col11(32'h87d000), .col12(32'h87cf00), .col13(32'h107c080), .col14(32'h1038080),
    .col15(32'h1001880), .col16(32'h1001880), .col17(32'h1038080), .col18(32'h107c080), .col19(32'h87cf00),
    .col20(32'h87d000), .col21(32'h439000), .col22(32'h382000), .col23(32'h7c000), .col24({32{1'b0}}),
    .col25({32{1'b0}}), .col26({32{1'b0}}), .col27({32{1'b0}}), .col28({32{1'b0}}), .col29({32{1'b0}}),
    .col30({32{1'b0}}), .col31({32{1'b0}}));
endmodule
